# Fritzing sketch FireTruck (saved by Fritzing 1.0.5)
breadboards: 1

parts:
  Part1 = Arduino Uno (Rev3) - ICSP
  Part3 = NRF24L01+ Breakout Board
  Part4 = NRF24L01+ Breakout Board
  L298N1 = L298N DC motor driver
  M1 = DC Motor [voltage_(max)=6V voltage_(min)=3V]  # not connected
  M2 = DC Motor [voltage_(max)=6V voltage_(min)=3V]  # not connected
  Part5 = Thumb Joystick
  BAT1 = LIPO-1000mAh [package=lipo-1000]
  BAT2 = LIPO-1000mAh [package=lipo-1000]
  R1 = Resistor [tolerance=±5% power=0.25W resistance=15k package=THT]
  R2 = Resistor [tolerance=±5% power=0.25W resistance=10k package=THT]
  LED1 = LED - 3mm [color="White (4500K)" current=0.030A package="3 mm [THT]"]
  LED2 = LED - 3mm [color="White (4500K)" current=0.030A package="3 mm [THT]"]
  LED3 = LED - 3mm [color="Blue (505nm)" current=0.030A package="3 mm [THT]"]
  LED4 = LED - 3mm [color="Blue (505nm)" current=0.030A package="3 mm [THT]"]
  LED5 = LED - 3mm [color="Red (660nm)" current=0.030A package="3 mm [THT]"]
  LED6 = LED - 3mm [color="Red (660nm)" current=0.030A package="3 mm [THT]"]
  R3 = Resistor [tolerance=±5% power=0.25W resistance=220 package=THT]
  R4 = Resistor [tolerance=±5% power=0.25W resistance=220 package=THT]
  R5 = Resistor [tolerance=±5% power=0.25W resistance=220 package=THT]
  R6 = Resistor [tolerance=±5% power=0.25W resistance=220 package=THT]
  R7 = Resistor [tolerance=±5% power=0.25W resistance=220 package=THT]
  R8 = Resistor [tolerance=±5% power=0.25W resistance=220 package=THT]
  Part6 = Arduino Mega 2560 (Rev3)
  S1 = SPST Switch [package=switch-spdt_lock.007s]

nets:
  N1: Part1.A0, Part5.VERT
  N2: Part1.A1, Part5.SEL
  N3: Part1.ICSP_MOSI, Part1.D11_PWM/MOSI, Part3.MOSI
  N4: Part1.D8, Part3.CS
  N5: Part1.D12/MISO, Part3.MISO
  N6: Part1.D13/SCK, Part3.SCK
  GND: Part1.GND, Part3.GND, Part5.GND
  N7: Part1.D2, Part5.HORZ
  N8: Part1.D7, Part3.CE
  3V3: Part1.3V3, Part3.VCC
  5V: Part1.5V, Part5.VCC
  GND_2: Part4.GND, Part6.GND
  VCC: Part4.VCC, Part6.3V3
  N9: Part4.CE, Part6.D7_PWM
  N10: Part4.CS, Part6.D8_PWM
  N11: Part4.SCK, Part6.D52
  N12: Part4.MOSI, Part6.D51
  N13: Part4.MISO, Part6.D50
  N14: L298N1.12V, R1.Pin_1, S1.P
  N15: L298N1.GND, BAT2.-, R2.Pin_1
  N16: L298N1.5V#9, L298N1.ENA
  N17: L298N1.5V#10, L298N1.ENB
  N18: BAT1.+, S1.O
  N19: BAT1.-, BAT2.+
  N20: R1.Pin_0, R2.Pin_0, Part6.A1
  N21: LED1.cathode, Part6.D22
  N22: LED1.anode, R3.Pin_0
  N23: LED2.cathode, Part6.D23
  N24: LED2.anode, R4.Pin_0
  N25: LED3.cathode, Part6.D24
  N26: LED3.anode, R5.Pin_0
  N27: LED4.cathode, Part6.D25
  N28: LED4.anode, R6.Pin_0
  N29: LED5.cathode, Part6.D26
  N30: LED5.anode, R7.Pin_0
  N31: LED6.cathode, Part6.D27
  N32: LED6.anode, R8.Pin_0
  N33: R3.Pin_1, R4.Pin_1, R5.Pin_1, R6.Pin_1, R7.Pin_1, R8.Pin_1

custom parts:
  L298N DC motor driver: 2x DC motor driver with 78M05 positive voltage regulator (7..35 V) L298N: max 46 V, 2 A Set 5 V Enable jumper to enable 5 V regultor (needed for the L298N) and +5 V output at screw terminal or supply external +5 V at screw terminal Set ENA and/or ENB to +5 V to enable motor permanently or supply ENA and/or ENB with PWM signal IN1 and IN2 set rotation directory for motor A (OUT1/OUT2) IN2 and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

// code stored in the sketch: Untitled2.ino

